# Fritzing sketch Debounce_w_433Mhz_and_555Timer (saved by Fritzing 1.0.3b)
circuit board: 7cm x 4cm
breadboards: 1

parts:
  R2 = Resistor [tolerance=±5% power=0.25W resistance=1k package=THT]
  C1 = Ceramic Capacitor [capacitance=10nF voltage=35V package="100 mil [THT, multilayer]"]
  555_Timer = 555 Timer [package="DIP8 [THT]"]
  S1 = Pushbutton [package="[THT]"]
  Q1 = NPN-Transistor [package="TO92 [THT]"]
  R1 = Resistor [tolerance=±5% power=0.25W resistance=460k package=THT]
  QIACHIP_RX480E = male pin header, 7 pins [form="♂ (male)"]
  Voltage_Regulator_5v = Voltage Regulator - 5V [package="TO220 [THT]"]
  R3 = Resistor [tolerance=±5% power=0.25W resistance=10k package=THT]
  C2 = Ceramic Capacitor [capacitance=0.1µF voltage=35V package="100 mil [THT, multilayer]"]
  R4 = Resistor [tolerance=±5% power=0.25W resistance=220 package=THT]
  D1 = Rectifier Diode [part_number=1N4001 package="300 mil [THT]"]
  D2 = Rectifier Diode [part_number=1N4001 package="300 mil [THT]"]
  C3 = Ceramic Capacitor [capacitance=0.1µF voltage=35V package="100 mil [THT, multilayer]"]
  VCC1 = Battery block 9V [internal_resistance=0.1Ω]
  Voltage_Regulator_3_3v = Voltage Regulator -- 3.3 V -- LM1117
  vIN_9-12v = molex pin header, 2 pins [form=molex part_number="JST B2B-XH-A"]
  3v_GPIO_IN = molex pin header, 2 pins [form=molex part_number="JST B2B-XH-A"]
  vOUT_3_3v = molex pin header, 2 pins [form=molex part_number="JST B2B-XH-A"]
  ext_Switch = molex pin header, 2 pins [form=molex part_number="JST B2B-XH-A"]

nets:
  N1: R2.Pin_0, 555_Timer.Trigger, 555_Timer.Threshold, R3.Pin_0, C2.0
  N2: R2.Pin_1, S1.Pin_3, S1.Pin_4, Q1.C, ext_Switch.pin1
  GND: C1.0, 555_Timer.Ground, S1.Pin_1, S1.Pin_2, Q1.E, QIACHIP_RX480E.pin1, Voltage_Regulator_5v.GND, C2.1, C3.0, VCC1.-, Voltage_Regulator_3_3v.GND, vIN_9-12v.pin2, 3v_GPIO_IN.pin2, vOUT_3_3v.pin2, ext_Switch.pin2
  N3: C1.1, 555_Timer.Control_Voltage
  N4: 555_Timer.Output, Voltage_Regulator_3_3v.IN
  N5: 555_Timer.Reset, 555_Timer.Vcc_Supply_Voltage, Voltage_Regulator_5v.input_voltage, R3.Pin_1, VCC1.+, vIN_9-12v.pin1
  N6: Q1.B, R1.Pin_1
  N7: R1.Pin_0, D1.cathode, D2.cathode
  N8: QIACHIP_RX480E.pin2, R4.Pin_0
  N9: QIACHIP_RX480E.pin4, D1.anode
  N10: Voltage_Regulator_5v.output_voltage, R4.Pin_1
  N11: D2.anode, 3v_GPIO_IN.pin1
  N12: C3.1, Voltage_Regulator_3_3v.OUT, vOUT_3_3v.pin1

notes:
  +
  -
  Debounce v1.0
  JST-3
  JST-1
  JST-2
  JST-4

custom parts:
  Voltage Regulator -- 3.3 V -- LM1117: LM1117-3.3 Voltage regulator, 3.3 V output. Note that the pinout order is not the same as LM7805 or LM7833.
