# Fritzing sketch neopixel_game (saved by Fritzing 1.0.3b)
circuit board: 7.76107cm x 4.20892cm
breadboards: 1

parts:
  U1 = TOUCH [package=touch2]
  S1 = SWITCH-MOMENTARY-2 [package=tactile-pth]
  U2 = WS2812 RGB LED strip
  J4 = Power Jack [package=power_jack_pth_lock]
  VCC1 = 4 x AAA Battery Mount [internal_resistance=0.1Ω]
  J1 = molex pin header, 2 pins [form=molex]
  R1 = Resistor [tolerance=±5% power=0.25W resistance=500 package=THT]
  R2 = Resistor [tolerance=±5% power=0.25W resistance=10000 package=THT]
  J2 = molex pin header, 3 pins [form=molex]
  C2 = Electrolytic Capacitor [capacitance=1mF voltage=35V package="200 mil [THT, electrolytic]"]
  esp8266_nodemcu = Amica NodeMCU DEVKIT 1.0

nets:
  N1: U1.T1, J1.pin2, esp8266_nodemcu.pin1, esp8266_nodemcu.pin_10, esp8266_nodemcu.pin_26
  N2: U1.T2, J1.pin1, R2.Pin_1, esp8266_nodemcu.pin_16
  GND: S1.1, U2.GND, J4.GND, VCC1.-, R2.Pin_0, J2.pin2, C2.-, esp8266_nodemcu.pin2, esp8266_nodemcu.pin_9, esp8266_nodemcu.pin_25, esp8266_nodemcu.pin_29
  N3: S1.2, esp8266_nodemcu.pin_11
  N4: U2.VCC, J4.GNDBREAK, VCC1.+, C2.+, esp8266_nodemcu.pin_30
  N5: U2.DIN, R1.Pin_0, J2.pin1
  N6: R1.Pin_1, esp8266_nodemcu.pin_15

notes:
  Neopixel
  Game
  v0.1

custom parts:
  WS2812 RGB LED strip: WS2812 strip
