# Fritzing sketch neopixel_game (saved by Fritzing 1.0.3b)
circuit board: 8.46667cm x 5.64444cm
breadboards: 1

parts:
  Mod1 = Amica NodeMCU DEVKIT 1.0
  U1 = TOUCH [package=touch2]
  S1 = SWITCH-MOMENTARY-2 [package=tactile-pth]
  J1 = female pin header, 2 pins [form="♀ (female)"]
  R1 = Resistor [tolerance=±5% resistance=500 package="2512 [SMD]"]
  R2 = Resistor [tolerance=±5% resistance=10000 package="2512 [SMD]"]
  U2 = WS2812 RGB LED strip
  J2 = female pin header, 2 pins [form="♀ (female)"]
  J4 = Power Jack [package=power_jack_pth_lock]
  C2 = Electrolytic Capacitor [capacitance=100µF voltage=35V package="200 mil [THT, electrolytic]"]
  VCC1 = 4 x AAA Battery Mount [internal_resistance=0.1Ω]

nets:
  N1: Mod1.pin1, Mod1.pin_10, Mod1.pin_26, U1.T1, J1.pin2
  GND: Mod1.pin2, Mod1.pin_9, Mod1.pin_25, Mod1.pin_29, S1.1, R2.Pin_0, U2.GND, J2.pin2, J4.GND, C2.-, VCC1.-
  N2: Mod1.pin_11, S1.2
  N3: Mod1.pin_15, R1.Pin_1
  N4: Mod1.pin_16, U1.T2, J1.pin1, R2.Pin_1
  N5: Mod1.pin_30, J4.GNDBREAK, C2.+, VCC1.+
  N6: R1.Pin_0, U2.DIN, J2.pin1

custom parts:
  WS2812 RGB LED strip: WS2812 strip
