# Fritzing sketch esp32_with_Neopixel (saved by Fritzing 1.0.3b)
circuit board: 6cm x 3.4cm
breadboards: 1

parts:
  lipo_3_7v = LIPO-110mAh [package=lipo-110]
  A_Neopixel = 12 NeoPixel Ring [part_number=1643]
  Tilt-2 = TILT-SWITCH-SW-200D [package=reed_switch_plastic]
  Tilt-1 = TILT-SWITCH-SW-200D [package=reed_switch_plastic]
  ESP32-S3_feather = Adafruit ESP32-S3 Feather [part_number="Adafruit #5323"]
  R3 = Rotary Potentiometer (Large) [maximum_resistance=10kΩ knob_status=50% power=0.5W package=THT]
  R1 = Resistor [tolerance=±5% resistance=10000 power=0.25W package=THT]
  R2 = Resistor [tolerance=±5% resistance=500 power=0.25W package=THT]
  J2 = molex pin header, 3 pins [form=molex]
  J1 = molex pin header, 2 pins [form=molex]

nets:
  VDD: lipo_3_7v.+, A_Neopixel.VDD, Tilt-2.1, Tilt-1.1, ESP32-S3_feather.3.3V, ESP32-S3_feather.VBAT, R3.leg2, J1.pin2
  GND: lipo_3_7v.-, A_Neopixel.GND, ESP32-S3_feather.GND, R3.leg1, R1.Pin_1, J1.pin1
  N1: A_Neopixel.IN, R2.Pin_1, J2.pin2
  N2: Tilt-2.2, Tilt-1.2, ESP32-S3_feather.D12, R1.Pin_0, J2.pin1
  N3: ESP32-S3_feather.SCL, ESP32-S3_feather.VBUS
  N4: ESP32-S3_feather.A5, R3.wiper, J2.pin3
  N5: ESP32-S3_feather.D6, R2.Pin_0

notes:
  W-remote
  V-0.0.2

custom parts:
  12 NeoPixel Ring: 12 ultra bright smart LED NeoPixels are arranged in a circle with 1.5" (37mm) outer diameter. The rings are 'chainable' - connect the output pin of one to the input pin of another. Use only one microcontroller pin to control as many as you can chain together! Each LED is addressable as the driver chip is inside the LED. Each one has ~18mA constant current drive so the color will be very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
  Adafruit ESP32-S3 Feather: The ESP32-S3 has arrived in Feather format - and what a great way to get started with this powerful new chip from Espressif! With dual 240 MHz cores, WiFi and BLE support, and native USB, this Feather is great for powering your IoT projects. That's right - it's the new Adafruit ESP32-S3 Feather! With native USB and 8 MB flash, this board will let you upgrade your existing ESP32 projects.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
